// Logisim project project1.circ as structural Verilog: 25 circuits, main circuit main
module main (
);

  wire button_1_out, clock_1_out, controller_1_alusrc, controller_1_extop, controller_1_luiop,
       controller_1_memtoreg, controller_1_memwrite, controller_1_npc_sel, controller_1_regdst,
       controller_1_regwrite, iszero_1_z;
  wire [1:0] controller_1_aluop;
  wire [4:0] alu_1_result, multiplexer_1_out;
  wire [15:0] ifu_offset_1_1_instr_2;
  wire [26:0] alu_1_result_2;
  wire [31:0] dm_1_memout, ext_1_result, gpr_1_rddata1, gpr_1_rddata2, multiplexer_2_out, multiplexer_3_out;
  wire [31:16] ifu_offset_1_1_instr;

  Clock clock_1 (.out(clock_1_out));
  // Probe on gpr_1_rddata1
  // Probe on multiplexer_2_out
  // Probe on {alu_1_result_2, alu_1_result}
  Button button_1 (.out(button_1_out));
  // Probe on {ifu_offset_1_1_instr, ifu_offset_1_1_instr_2}
  // Probe on {ifu_offset_1_1_instr, ifu_offset_1_1_instr_2}
  IFU_OFFSET_1 ifu_offset_1_1 (
    .IfBeq(controller_1_npc_sel), .Zero(iszero_1_z), .Reset(button_1_out), .Clk(clock_1_out),
    .Instr({ifu_offset_1_1_instr, ifu_offset_1_1_instr_2}));
  IFU ifu_1 ();  // open: IfBeq, Zero, Reset, Clk, Instr
  // Probe on ext_1_result
  Multiplexer #(.width(5)) multiplexer_1 (
    .in0(ifu_offset_1_1_instr[20:16]), .in1(ifu_offset_1_1_instr_2[15:11]), .out(multiplexer_1_out),
    .sel(controller_1_regdst));
  EXT ext_1 (.A(ifu_offset_1_1_instr_2), .Extop(controller_1_extop), .LuiOp(controller_1_luiop), .result(ext_1_result));
  Controller controller_1 (
    .op(ifu_offset_1_1_instr[31:26]), .func(ifu_offset_1_1_instr_2[5:0]), .RegDst(controller_1_regdst),
    .ALUSrc(controller_1_alusrc), .MemtoReg(controller_1_memtoreg), .RegWrite(controller_1_regwrite),
    .MemWrite(controller_1_memwrite), .nPC_sel(controller_1_npc_sel), .ExtOp(controller_1_extop),
    .LuiOp(controller_1_luiop), .ALUop(controller_1_aluop));
  // Probe on gpr_1_rddata2
  GPR gpr_1 (
    .Regrd1(ifu_offset_1_1_instr[25:21]), .Regrd2(ifu_offset_1_1_instr[20:16]), .A3(multiplexer_1_out),
    .clk(clock_1_out), .Reset(button_1_out), .Regwrite(controller_1_regwrite), .Wd(multiplexer_3_out),
    .Rddata1(gpr_1_rddata1), .Rddata2(gpr_1_rddata2));
  Multiplexer #(.width(32)) multiplexer_2 (
    .in0(gpr_1_rddata2), .in1(ext_1_result), .out(multiplexer_2_out), .sel(controller_1_alusrc));
  // Probe on ext_1_result
  // Probe on gpr_1_rddata1
  // Probe on multiplexer_2_out
  // Probe on multiplexer_2_out
  IsZero iszero_1 (.A({alu_1_result_2, alu_1_result}), .Z(iszero_1_z));
  ALU alu_1 (
    .op(controller_1_aluop), .A(gpr_1_rddata1), .B(multiplexer_2_out), .result({alu_1_result_2, alu_1_result}));
  // Probe on {alu_1_result_2, alu_1_result}
  DM dm_1 (
    .address(alu_1_result), .Data(gpr_1_rddata2), .Memtoreg(controller_1_memtoreg),
    .Memwrite(controller_1_memwrite), .Clk(clock_1_out), .Reset(button_1_out), .MEMout(dm_1_memout));
  Multiplexer #(.width(32)) multiplexer_3 (
    .in0({alu_1_result_2, alu_1_result}), .in1(dm_1_memout), .out(multiplexer_3_out),
    .sel(controller_1_memtoreg));
endmodule

module IFU (
  input  IfBeq,
  input  Zero,
  input  Reset,
  input  Clk,
  output [31:0] Instr
);

  wire and_1_out;
  wire [31:0] alu_1_result, alu_2_result, bit_extender_1_out, multiplexer_1_out, PC_q;

  Register #(.width(32)) PC (.D(alu_1_result), .en(1'b1), .clk(Clk), .Q(PC_q), .clr(Reset));
  ALU alu_1 (.op(2'b11), .A(PC_q), .B(alu_2_result), .result(alu_1_result));
  ROM #(.addrWidth(5), .dataWidth(32)) rom_1 (.addr(PC_q[4:0]), .data(Instr));
  and and_1 (and_1_out, IfBeq, Zero);
  Multiplexer #(.width(32)) multiplexer_1 (
    .in0(32'h1), .in1(bit_extender_1_out), .out(multiplexer_1_out), .sel(and_1_out));
  assign bit_extender_1_out = {{16{Instr[15]}}, Instr[15:0]};  // Bit_Extender bit_extender_1
  // Probe on Instr
  ALU alu_2 (.op(2'b11), .A(multiplexer_1_out), .B({32{1'b0}}), .result(alu_2_result));

  // Notes on the sheet:
  //   contents of rom_1 (hex, n*v repeats v):
  //   8d55000f 8ee40014 36b30008 34940010 274a821 293b023 3c11007f 3c1200ff 2511823 2322023 ad43000f
  //   aef40014 2739821 12740002 36b303ff 349403ff 3c1503ff ad150000 8d090000 1294821
endmodule

module add4 (
  input  A7,
  input  B7,
  input  A6,
  input  B6,
  input  A5,
  input  B5,
  input  A4,
  input  B4,
  input  A3,
  input  B3,
  input  A2,
  input  B2,
  input  A1,
  input  B1,
  input  A0,
  input  B0,
  input  C0,
  output Carry,
  output F7,
  output F6,
  output F5,
  output F4,
  output F3,
  output F2,
  output F1,
  output F0
);

  wire add1_2_carry, add1_3_carry, add1_4_carry, add1_5_carry, add1_6_carry, add1_7_carry, add1_8_carry;

  add1 add1_1 (.A(A7), .B(B7), .C0(add1_2_carry), .Carry(Carry), .F(F7));
  add1 add1_2 (.A(A6), .B(B6), .C0(add1_7_carry), .Carry(add1_2_carry), .F(F6));
  add1 add1_3 (.A(A4), .B(B4), .C0(add1_4_carry), .Carry(add1_3_carry), .F(F4));
  add1 add1_4 (.A(A3), .B(B3), .C0(add1_5_carry), .Carry(add1_4_carry), .F(F3));
  add1 add1_5 (.A(A2), .B(B2), .C0(add1_8_carry), .Carry(add1_5_carry), .F(F2));
  add1 add1_6 (.A(A0), .B(B0), .C0(C0), .Carry(add1_6_carry), .F(F0));
  add1 add1_7 (.A(A5), .B(B5), .C0(add1_3_carry), .Carry(add1_7_carry), .F(F5));
  add1 add1_8 (.A(A1), .B(B1), .C0(add1_6_carry), .Carry(add1_8_carry), .F(F1));
endmodule

module add1 (
  input  A,
  input  B,
  input  C0,
  output Carry,
  output F
);

  wire and_1_out, and_2_out, xor_1_out;

  and and_1 (and_1_out, A, B);
  xor xor_1 (xor_1_out, A, B);
  xor xor_2 (F, xor_1_out, C0);
  and and_2 (and_2_out, xor_1_out, C0);
  or or_1 (Carry, and_1_out, and_2_out);
endmodule

module add8 (
  input  A7,
  input  B7,
  input  A6,
  input  B6,
  input  A5,
  input  B5,
  input  A4,
  input  B4,
  input  A3,
  input  B3,
  input  A2,
  input  B2,
  input  A1,
  input  B1,
  input  A0,
  input  B0,
  input  C0,
  output Carry,
  output F7,
  output F6,
  output F5,
  output F4,
  output F3,
  output F2,
  output F1,
  output F0
);

  wire add1_2_carry, add1_3_carry, add1_4_carry, add1_5_carry, add1_6_carry, add1_7_carry, add1_8_carry;

  add1 add1_1 (.A(A7), .B(B7), .C0(add1_2_carry), .Carry(Carry), .F(F7));
  add1 add1_2 (.A(A6), .B(B6), .C0(add1_3_carry), .Carry(add1_2_carry), .F(F6));
  add1 add1_3 (.A(A5), .B(B5), .C0(add1_4_carry), .Carry(add1_3_carry), .F(F5));
  add1 add1_4 (.A(A4), .B(B4), .C0(add1_5_carry), .Carry(add1_4_carry), .F(F4));
  add1 add1_5 (.A(A3), .B(B3), .C0(add1_6_carry), .Carry(add1_5_carry), .F(F3));
  add1 add1_6 (.A(A2), .B(B2), .C0(add1_7_carry), .Carry(add1_6_carry), .F(F2));
  add1 add1_7 (.A(A1), .B(B1), .C0(add1_8_carry), .Carry(add1_7_carry), .F(F1));
  add1 add1_8 (.A(A0), .B(B0), .C0(C0), .Carry(add1_8_carry), .F(F0));
endmodule

module add16_wrong (
  input  A15,
  input  A7,
  input  B15,
  input  B7,
  input  A14,
  input  A6,
  input  B14,
  input  B6,
  input  A13,
  input  A5,
  input  B13,
  input  B5,
  input  A12,
  input  A4,
  input  B12,
  input  B4,
  input  A11,
  input  A3,
  input  B11,
  input  B3,
  input  A10,
  input  A2,
  input  B10,
  input  B2,
  input  A9,
  input  A1,
  input  B9,
  input  B1,
  input  A8,
  input  A0,
  input  B8,
  input  B0,
  input  C0,
  output F7,
  output F15,
  output F6,
  output F14,
  output F5,
  output F13,
  output F4,
  output F12,
  output F3,
  output F11,
  output F2,
  output F10,
  output F1,
  output F9,
  output F0,
  output F8
);

  wire add8_1_carry;

  add8 add8_1 (
    .A7(A7), .B7(B7), .A6(A6), .B6(B6), .A5(A5), .B5(B5), .A4(A4), .B4(B4), .A3(A3), .B3(B3), .A2(A2),
    .B2(B2), .A1(A1), .B1(B1), .A0(A0), .B0(B0), .C0(C0), .Carry(add8_1_carry), .F7(F7), .F6(F6), .F5(F5),
    .F4(F4), .F3(F3), .F2(F2), .F1(F1), .F0(F0));
  add8 add8_2 (
    .A7(A15), .B7(B15), .A6(A14), .B6(B14), .A5(A13), .B5(B13), .A4(A12), .B4(B12), .A3(A11), .B3(B11),
    .A2(A10), .B2(B10), .A1(A9), .B1(B9), .A0(A8), .B0(B8), .C0(add8_1_carry), .F7(F15), .F6(F14), .F5(F13),
    .F4(F12), .F3(F11), .F2(F10), .F1(F9), .F0(F8));  // open: Carry
endmodule

module test (
  input  in_1,
  input  [31:0] in_2,
  input  [31:0] in_3,
  input  [1:0] op,
  input  [31:0] in_5,
  input  [31:0] in_6,
  input  [7:0] in_7,
  input  in_8,
  input  in_9,
  input  in_10,
  input  in_11,
  input  in_12,
  input  in_13,
  input  in_14,
  input  in_15,
  input  in_16,
  input  in_17,
  input  in_18,
  input  in_19,
  input  [15:0] in_20,
  input  [15:0] in_21,
  input  in_22,
  input  [7:0] in_23,
  input  in_24,
  input  [7:0] in_25,
  input  in_26,
  output out_27,
  output [31:0] out_28,
  output [31:0] out_29,
  output [7:0] out_30,
  output [31:0] A1,
  output out_32,
  output out_33,
  output out_34,
  output out_35,
  output out_36,
  output out_37,
  output [15:0] out_38
);

  wire [7:0] register_1_q, register_3_q, register_4_q;

  Register register_1 (.D(in_23), .clk(in_24), .Q(register_1_q));  // open: en, clr
  Register register_2 (.D(in_7), .en(in_8), .clk(in_9), .Q(out_30), .clr(in_10));
  GPR gpr_1 ();  // open: Regrd1, Regrd2, A3, clk, Reset, Regwrite, Wd, Rddata1, Rddata2
  Register register_3 (.D(register_1_q), .clk(in_24), .Q(register_3_q));  // open: en, clr
  Register register_4 (.D(in_25), .clk(in_26), .Q(register_4_q));  // open: en, clr
  // Probe on register_3_q
  // Probe on register_4_q
  ALU alu_1 (.op(op), .A(in_5), .B(in_6), .result(out_29));
  add32 add32_1 (.A(in_2), .B(in_3), .C0(in_1), .result(out_28));
  lookahead_add4 lookahead_add4_1 (
    .A4(in_11), .A3(in_12), .A2(in_13), .A1(in_14), .B4(in_15), .B3(in_16), .B2(in_17), .B1(in_18),
    .C0(in_19), .Cout(out_32), .S4(out_33), .S3(out_34), .S2(out_35), .S1(out_36));  // open: P, G
  lookahead_add16 lookahead_add16_1 (.A(in_20), .B(in_21), .C0(in_22), .Carry(out_37), .S(out_38));
endmodule

module add16 (
  input  [15:0] A,
  input  [15:0] B,
  input  C0,
  output Carry,
  output [15:0] F
);

  wire add8_1_carry;

  add8 add8_1 (
    .A7(A[7]), .B7(B[7]), .A6(A[6]), .B6(B[6]), .A5(A[5]), .B5(B[5]), .A4(A[4]), .B4(B[4]), .A3(A[3]),
    .B3(B[3]), .A2(A[2]), .B2(B[2]), .A1(A[1]), .B1(B[1]), .A0(A[0]), .B0(B[0]), .C0(C0),
    .Carry(add8_1_carry), .F7(F[7]), .F6(F[6]), .F5(F[5]), .F4(F[4]), .F3(F[3]), .F2(F[2]), .F1(F[1]),
    .F0(F[0]));
  add8 add8_2 (
    .A7(A[15]), .B7(B[15]), .A6(A[14]), .B6(B[14]), .A5(A[13]), .B5(B[13]), .A4(A[12]), .B4(B[12]),
    .A3(A[11]), .B3(B[11]), .A2(A[10]), .B2(B[10]), .A1(A[9]), .B1(B[9]), .A0(A[8]), .B0(B[8]),
    .C0(add8_1_carry), .Carry(Carry), .F7(F[15]), .F6(F[14]), .F5(F[13]), .F4(F[12]), .F3(F[11]), .F2(F[10]),
    .F1(F[9]), .F0(F[8]));
endmodule

module add32 (
  input  [31:0] A,
  input  [31:0] B,
  input  C0,
  output [31:0] result
);

  wire add16_1_carry, add16_2_carry;

  add16 add16_1 (.A(A[31:16]), .B(B[31:16]), .C0(add16_2_carry), .Carry(add16_1_carry), .F(result[31:16]));
  add16 add16_2 (.A(A[15:0]), .B(B[15:0]), .C0(C0), .Carry(add16_2_carry), .F(result[15:0]));
endmodule

module or32 (
  input  [31:0] A,
  input  [31:0] B,
  output [31:0] result
);

  assign result = A | B;  // OR_Gate or_1, 32 bits wide
endmodule

module ALU (
  input  [1:0] op,
  input  [31:0] A,
  input  [31:0] B,
  output [31:0] result
);

  wire not_2_out;
  wire [31:0] add32_1_result, multiplexer_1_out, not_1_out, or32_1_result;

  assign not_1_out = ~B;  // NOT_Gate not_1, 32 bits wide
  Multiplexer #(.width(32)) multiplexer_1 (.in0(not_1_out), .in1(B), .out(multiplexer_1_out), .sel(op[0]));
  not not_2 (not_2_out, op[0]);
  or32 or32_1 (.A(A), .B(B), .result(or32_1_result));
  add32 add32_1 (.A(A), .B(multiplexer_1_out), .C0(not_2_out), .result(add32_1_result));
  Multiplexer #(.width(32)) multiplexer_2 (.in0(or32_1_result), .in1(add32_1_result), .out(result), .sel(op[1]));
endmodule

module EXT (
  input  [15:0] A,
  input  Extop,
  input  LuiOp,
  output [31:0] result
);

  wire [31:0] bit_extender_1_out, bit_extender_2_out, multiplexer_1_out;

  assign bit_extender_1_out = {{16{1'b0}}, A};  // Bit_Extender bit_extender_1
  assign bit_extender_2_out = {{16{A[15]}}, A};  // Bit_Extender bit_extender_2
  Multiplexer #(.width(32)) multiplexer_1 (
    .in0(bit_extender_1_out), .in1(bit_extender_2_out), .out(multiplexer_1_out), .sel(Extop));
  Multiplexer #(.width(32)) multiplexer_2 (
    .in0(multiplexer_1_out), .in1({multiplexer_1_out[15:0], multiplexer_1_out[31:16]}), .out(result),
    .sel(LuiOp));
endmodule

module DM (
  input  [4:0] address,
  input  [31:0] Data,
  input  Memtoreg,
  input  Memwrite,
  input  Clk,
  input  Reset,
  output [31:0] MEMout
);

  RAM #(.addrWidth(5), .asyncread("true"), .clearpin("true"), .dataWidth(32)) ram_1 (
    .addr(address), .we(Memwrite), .oe(Memtoreg), .clk(Clk), .din(Data), .dout(MEMout), .clr(Reset));
endmodule

module GPR (
  input  [4:0] Regrd1,
  input  [4:0] Regrd2,
  input  [4:0] A3,
  input  clk,
  input  Reset,
  input  Regwrite,
  input  [31:0] Wd,
  output [31:0] Rddata1,
  output [31:0] Rddata2
);

  wire WR0, WR1, WR2, WR3, WR4, WR5, WR6, WR7, WR8, WR9, WR10, WR11, WR12, WR13, WR14, WR15, WR16, WR17,
       WR18, WR19, WR20, WR21, WR22, WR23, WR24, WR25, WR26, WR27, WR28, WR29, WR30, WR31;
  wire [31:0] RD0, RD1, RD2, RD3, RD4, RD5, RD6, RD7, RD8, RD9, RD10, RD11, RD12, RD13, RD14, RD15, RD16,
       RD17, RD18, RD19, RD20, RD21, RD22, RD23, RD24, RD25, RD26, RD27, RD28, RD29, RD30, RD31;

  Decoder #(.select(5)) decoder_1 (
    .out0(WR0), .out1(WR1), .out2(WR2), .out3(WR3), .out4(WR4), .out5(WR5), .out6(WR6), .out7(WR7),
    .out8(WR8), .out9(WR9), .out10(WR10), .out11(WR11), .out12(WR12), .out13(WR13), .out14(WR14),
    .out15(WR15), .out16(WR16), .out17(WR17), .out18(WR18), .out19(WR19), .out20(WR20), .out21(WR21),
    .out22(WR22), .out23(WR23), .out24(WR24), .out25(WR25), .out26(WR26), .out27(WR27), .out28(WR28),
    .out29(WR29), .out30(WR30), .out31(WR31), .sel(A3), .en(Regwrite));
  Multiplexer #(.select(5), .width(32)) multiplexer_1 (
    .in0(RD0), .in1(RD1), .in2(RD2), .in3(RD3), .in4(RD4), .in5(RD5), .in6(RD6), .in7(RD7), .in8(RD8),
    .in9(RD9), .in10(RD10), .in11(RD11), .in12(RD12), .in13(RD13), .in14(RD14), .in15(RD15), .in16(RD16),
    .in17(RD17), .in18(RD18), .in19(RD19), .in20(RD20), .in21(RD21), .in22(RD22), .in23(RD23), .in24(RD24),
    .in25(RD25), .in26(RD26), .in27(RD27), .in28(RD28), .in29(RD29), .in30(RD30), .in31(RD31), .out(Rddata1),
    .sel(Regrd1));
  Multiplexer #(.select(5), .width(32)) multiplexer_2 (
    .in0(RD0), .in1(RD1), .in2(RD2), .in3(RD3), .in4(RD4), .in5(RD5), .in6(RD6), .in7(RD7), .in8(RD8),
    .in9(RD9), .in10(RD10), .in11(RD11), .in12(RD12), .in13(RD13), .in14(RD14), .in15(RD15), .in16(RD16),
    .in17(RD17), .in18(RD18), .in19(RD19), .in20(RD20), .in21(RD21), .in22(RD22), .in23(RD23), .in24(RD24),
    .in25(RD25), .in26(RD26), .in27(RD27), .in28(RD28), .in29(RD29), .in30(RD30), .in31(RD31), .out(Rddata2),
    .sel(Regrd2));
  Register #(.width(32)) register_1 (.D(Wd), .en(WR0), .clk(clk), .Q(RD0), .clr(Reset));
  Register #(.width(32)) register_2 (.D(Wd), .en(WR1), .clk(clk), .Q(RD1), .clr(Reset));
  Register #(.width(32)) register_3 (.D(Wd), .en(WR2), .clk(clk), .Q(RD2), .clr(Reset));
  Register #(.width(32)) register_4 (.D(Wd), .en(WR3), .clk(clk), .Q(RD3), .clr(Reset));
  Register #(.width(32)) register_5 (.D(Wd), .en(WR4), .clk(clk), .Q(RD4), .clr(Reset));
  Register #(.width(32)) register_6 (.D(Wd), .en(WR5), .clk(clk), .Q(RD5), .clr(Reset));
  Register #(.width(32)) register_7 (.D(Wd), .en(WR6), .clk(clk), .Q(RD6), .clr(Reset));
  Register #(.width(32)) register_8 (.D(Wd), .en(WR7), .clk(clk), .Q(RD7), .clr(Reset));
  Register #(.width(32)) register_9 (.D(Wd), .en(WR8), .clk(clk), .Q(RD8), .clr(Reset));
  Register #(.width(32)) register_10 (.D(Wd), .en(WR9), .clk(clk), .Q(RD9), .clr(Reset));
  Register #(.width(32)) register_11 (.D(Wd), .en(WR10), .clk(clk), .Q(RD10), .clr(Reset));
  Register #(.width(32)) register_12 (.D(Wd), .en(WR11), .clk(clk), .Q(RD11), .clr(Reset));
  Register #(.width(32)) register_13 (.D(Wd), .en(WR12), .clk(clk), .Q(RD12), .clr(Reset));
  Register #(.width(32)) register_14 (.D(Wd), .en(WR13), .clk(clk), .Q(RD13), .clr(Reset));
  Register #(.width(32)) register_15 (.D(Wd), .en(WR14), .clk(clk), .Q(RD14), .clr(Reset));
  Register #(.width(32)) register_16 (.D(Wd), .en(WR15), .clk(clk), .Q(RD15), .clr(Reset));
  Register #(.width(32)) register_17 (.D(Wd), .en(WR16), .clk(clk), .Q(RD16), .clr(Reset));
  Register #(.width(32)) register_18 (.D(Wd), .en(WR17), .clk(clk), .Q(RD17), .clr(Reset));
  Register #(.width(32)) register_19 (.D(Wd), .en(WR18), .clk(clk), .Q(RD18), .clr(Reset));
  Register #(.width(32)) register_20 (.D(Wd), .en(WR19), .clk(clk), .Q(RD19), .clr(Reset));
  Register #(.width(32)) register_21 (.D(Wd), .en(WR20), .clk(clk), .Q(RD20), .clr(Reset));
  Register #(.width(32)) register_22 (.D(Wd), .en(WR21), .clk(clk), .Q(RD21), .clr(Reset));
  Register #(.width(32)) register_23 (.D(Wd), .en(WR22), .clk(clk), .Q(RD22), .clr(Reset));
  Register #(.width(32)) register_24 (.D(Wd), .en(WR23), .clk(clk), .Q(RD23), .clr(Reset));
  Register #(.width(32)) register_25 (.D(Wd), .en(WR24), .clk(clk), .Q(RD24), .clr(Reset));
  Register #(.width(32)) register_26 (.D(Wd), .en(WR25), .clk(clk), .Q(RD25), .clr(Reset));
  Register #(.width(32)) register_27 (.D(Wd), .en(WR26), .clk(clk), .Q(RD26), .clr(Reset));
  Register #(.width(32)) register_28 (.D(Wd), .en(WR27), .clk(clk), .Q(RD27), .clr(Reset));
  Register #(.width(32)) register_29 (.D(Wd), .en(WR28), .clk(clk), .Q(RD28), .clr(Reset));
  Register #(.width(32)) register_30 (.D(Wd), .en(WR29), .clk(clk), .Q(RD29), .clr(Reset));
  Register #(.width(32)) register_31 (.D(Wd), .en(WR30), .clk(clk), .Q(RD30), .clr(Reset));
  Register #(.width(32)) register_32 (.D(Wd), .en(WR31), .clk(clk), .Q(RD31), .clr(Reset));
endmodule

module Controller_mistaken (
  input  [5:0] op
);

  wire ALUsrc_out, and_1_out, and_2_out, and_3_out, not_1_out, not_2_out, not_3_out, not_4_out, not_5_out,
       not_6_out, not_7_out, not_8_out, not_9_out, not_10_out, not_11_out, not_12_out, not_13_out,
       not_14_out, not_15_out, not_16_out, Regdst_And_out;

  not not_1 (not_1_out, op[0]);
  not not_2 (not_2_out, op[1]);
  not not_3 (not_3_out, op[2]);
  not not_4 (not_4_out, op[3]);
  not not_5 (not_5_out, op[4]);
  not not_6 (not_6_out, op[5]);
  and Regdst_And (Regdst_And_out, not_6_out, not_5_out, not_4_out, not_3_out, not_2_out, not_1_out);
  not not_7 (not_7_out, not_4_out);
  not not_8 (not_8_out, not_3_out);
  and and_1 (and_1_out, not_6_out, not_5_out, not_7_out, not_8_out, not_2_out, not_9_out);
  not not_9 (not_9_out, not_1_out);
  not not_10 (not_10_out, not_6_out);
  not not_11 (not_11_out, not_2_out);
  not not_12 (not_12_out, not_1_out);
  and and_2 (and_2_out, not_10_out, not_5_out, not_4_out, not_3_out, not_11_out, not_12_out);
  or ALUsrc (ALUsrc_out, and_1_out, and_2_out, and_3_out);
  not not_13 (not_13_out, not_6_out);
  not not_14 (not_14_out, not_4_out);
  not not_15 (not_15_out, not_2_out);
  not not_16 (not_16_out, not_1_out);
  and and_3 (and_3_out, not_13_out, not_5_out, not_14_out, not_3_out, not_15_out, not_16_out);
endmodule

module Controller (
  input  [5:0] op,
  input  [5:0] func,
  output RegDst,
  output ALUSrc,
  output MemtoReg,
  output RegWrite,
  output MemWrite,
  output nPC_sel,
  output ExtOp,
  output LuiOp,
  output [1:0] ALUop
);

  wire ADDU_out, and_1_out, not_2_out, not_3_out, not_4_out, not_5_out, not_6_out, not_7_out, not_8_out,
       not_9_out, not_10_out, not_11_out, ori_out, SUBU_out;

  // NOT_Gate not_1 is placed but not wired
  not not_2 (not_2_out, func[2]);
  not not_3 (not_3_out, func[3]);
  not not_4 (not_4_out, func[4]);
  or or_1 (ALUop[0], MemWrite, MemtoReg, ori_out, ADDU_out);
  not not_5 (not_5_out, op[0]);
  not not_6 (not_6_out, op[1]);
  not not_7 (not_7_out, op[3]);
  not not_8 (not_8_out, op[4]);
  not not_9 (not_9_out, op[5]);
  not not_10 (not_10_out, func[1]);
  and ADDU (ADDU_out, and_1_out, func[5], not_4_out, not_3_out, not_2_out, not_10_out, func[0]);
  not not_11 (not_11_out, op[2]);
  and SUBU (SUBU_out, and_1_out, func[5], not_4_out, not_3_out, not_2_out, func[1], func[0]);
  or or_2 (ALUop[1], ADDU_out, MemtoReg, nPC_sel, MemWrite, SUBU_out);
  and and_1 (and_1_out, not_9_out, not_8_out, not_7_out, not_11_out, not_6_out, not_5_out);
  or or_3 (RegDst, SUBU_out, ADDU_out);
  and ori (ori_out, not_9_out, not_8_out, op[3], op[2], not_6_out, op[0]);
  or or_4 (ALUSrc, ori_out, MemtoReg, MemWrite, LuiOp);
  and lw (MemtoReg, op[5], not_8_out, not_7_out, not_11_out, op[1], op[0]);
  or or_5 (RegWrite, ADDU_out, SUBU_out, LuiOp, ori_out, MemtoReg);
  and sw (MemWrite, op[5], not_8_out, op[3], not_11_out, op[1], op[0]);
  and beq (nPC_sel, not_9_out, not_8_out, not_7_out, op[2], not_6_out, not_5_out);
  or or_6 (ExtOp, MemtoReg, MemWrite);
  and lui (LuiOp, not_9_out, not_8_out, op[3], op[2], op[1], op[0]);
endmodule

module IsZero (
  input  [31:0] A,
  output Z
);

  wire or_1_out;

  or or_1 (or_1_out, A[15], A[0], A[1], A[2], A[3], A[4], A[5], A[6], A[7], A[8], A[9], A[10], A[11], A[12], A[13], A[14], A[16], A[17], A[18], A[19], A[20], A[21], A[22], A[23], A[24], A[25], A[26], A[27], A[28], A[29], A[30], A[31]);
  not not_1 (Z, or_1_out);
endmodule

module IFU_OFFSET_1 (
  input  IfBeq,
  input  Zero,
  input  Reset,
  input  Clk,
  output [31:0] Instr
);

  wire and_1_out;
  wire [31:0] alu_1_result, alu_2_result, bit_extender_1_out, multiplexer_1_out, PC_q;

  Register #(.width(32)) PC (.D(multiplexer_1_out), .en(1'b1), .clk(Clk), .Q(PC_q), .clr(Reset));
  ALU alu_1 (.op(2'b11), .A(PC_q), .B(32'h1), .result(alu_1_result));
  ROM #(.addrWidth(5), .dataWidth(32)) rom_1 (.addr(PC_q[4:0]), .data(Instr));
  and and_1 (and_1_out, IfBeq, Zero);
  Multiplexer #(.width(32)) multiplexer_1 (
    .in0(alu_1_result), .in1(alu_2_result), .out(multiplexer_1_out), .sel(and_1_out));
  assign bit_extender_1_out = {{16{Instr[15]}}, Instr[15:0]};  // Bit_Extender bit_extender_1
  // Probe on Instr
  ALU alu_2 (.op(2'b11), .A(alu_1_result), .B(bit_extender_1_out), .result(alu_2_result));

  // Notes on the sheet:
  //   contents of rom_1 (hex, n*v repeats v):
  //   341a0001 34211111 34422222 34633333 232021 812823 3c066666 34c66666 3c07ffff 34e7ffff f9c823
  //   10f90001 3c080059 1615821 3c010000 34210001 1415021 115afffb 35ef0001 36100002 20f8823 22f9021
  //   2129823 ae41000a ae030002 ae660010 8e34000b 36b50000 8df6000f 8c170004
endmodule

module lookahead_add4 (
  input  A4,
  input  A3,
  input  A2,
  input  A1,
  input  B4,
  input  B3,
  input  B2,
  input  B1,
  input  C0,
  output Cout,
  output S4,
  output S3,
  output S2,
  output S1,
  output P,
  output G
);

  wire and_2_out, and_3_out, and_4_out, and_5_out, and_6_out, and_7_out, and_8_out, and_9_out, and_10_out,
       C1_out, C2_out, C3_out, G1_out, G2_out, G3_out, G4_out, P1_out, P2_out, P3_out, P4_out;

  xor P4 (P4_out, A4, B4);
  xor P3 (P3_out, A3, B3);
  xor P2 (P2_out, A2, B2);
  xor P1 (P1_out, A1, B1);
  and G4 (G4_out, A4, B4);
  and G3 (G3_out, A3, B3);
  and G2 (G2_out, A2, B2);
  and G1 (G1_out, A1, B1);
  and and_1 (P, P4_out, P3_out, P2_out, P1_out, C0);
  and and_2 (and_2_out, P4_out, P3_out, P2_out, G1_out);
  and and_3 (and_3_out, P4_out, P3_out, G2_out);
  and and_4 (and_4_out, P4_out, G3_out);
  and and_5 (and_5_out, P3_out, G2_out);
  and and_6 (and_6_out, P3_out, P2_out, P1_out, C0);
  and and_7 (and_7_out, P3_out, P2_out, G1_out);
  and and_8 (and_8_out, P1_out, C0);
  xor xor_1 (S1, P1_out, C0);
  or C1 (C1_out, and_8_out, G1_out);
  and and_9 (and_9_out, P2_out, G1_out);
  and and_10 (and_10_out, P2_out, C0, P1_out);
  xor xor_2 (S2, P2_out, C1_out);
  or C3 (C3_out, and_5_out, and_6_out, and_7_out, G3_out);
  or C2 (C2_out, and_9_out, and_10_out, G2_out);
  xor xor_3 (S4, P4_out, C3_out);
  xor xor_4 (S3, P3_out, C2_out);
  or or_1 (G, and_2_out, G4_out, and_4_out, and_3_out);
  or or_2 (Cout, P, G);
endmodule

module lookahead_add16 (
  input  [15:0] A,
  input  [15:0] B,
  input  C0,
  output Carry,
  output [15:0] S
);

  wire aa1_g, aa1_p, aa2_g, aa2_p, aa3_g, aa3_p, aa4_g, aa4_p, and_1_out, and_2_out, and_3_out, and_4_out,
       and_5_out, and_6_out, and_7_out, and_8_out, and_9_out, and_10_out, C1_out, C2_out, C3_out;

  lookahead_add4 aa4 (
    .A4(A[15]), .A3(A[14]), .A2(A[13]), .A1(A[12]), .B4(B[15]), .B3(B[14]), .B2(B[13]), .B1(B[12]),
    .C0(C3_out), .S4(S[15]), .S3(S[14]), .S2(S[13]), .S1(S[12]), .P(aa4_p), .G(aa4_g));  // open: Cout
  lookahead_add4 aa3 (
    .A4(A[11]), .A3(A[10]), .A2(A[9]), .A1(A[8]), .B4(B[11]), .B3(B[10]), .B2(B[9]), .B1(B[8]), .C0(C2_out),
    .S4(S[11]), .S3(S[10]), .S2(S[9]), .S1(S[8]), .P(aa3_p), .G(aa3_g));  // open: Cout
  lookahead_add4 aa2 (
    .A4(A[7]), .A3(A[6]), .A2(A[5]), .A1(A[4]), .B4(B[7]), .B3(B[6]), .B2(B[5]), .B1(B[4]), .C0(C1_out),
    .S4(S[7]), .S3(S[6]), .S2(S[5]), .S1(S[4]), .P(aa2_p), .G(aa2_g));  // open: Cout
  lookahead_add4 aa1 (
    .A4(A[3]), .A3(A[2]), .A2(A[1]), .A1(A[0]), .B4(B[3]), .B3(B[2]), .B2(B[1]), .B1(B[0]), .C0(C0),
    .S4(S[3]), .S3(S[2]), .S2(S[1]), .S1(S[0]), .P(aa1_p), .G(aa1_g));  // open: Cout
  and and_1 (and_1_out, aa1_p, C0);
  or C1 (C1_out, and_1_out, aa1_g);
  and and_2 (and_2_out, aa4_p, aa3_p, aa2_p, aa1_p, C0);
  and and_3 (and_3_out, aa4_p, aa3_p, aa2_p, aa1_g);
  and and_4 (and_4_out, aa4_p, aa3_p, aa2_g);
  and and_5 (and_5_out, aa4_p, aa3_g);
  and and_6 (and_6_out, aa3_p, aa2_p, aa1_p, C0);
  and and_7 (and_7_out, aa3_p, aa2_p, aa1_g);
  and and_8 (and_8_out, aa3_p, aa2_g);
  and and_9 (and_9_out, aa2_p, aa1_p, C0);
  and and_10 (and_10_out, aa2_p, aa1_g);
  or C3 (C3_out, and_6_out, and_7_out, and_8_out, aa3_g);
  or C2 (C2_out, and_9_out, and_10_out, aa2_g);
  or or_1 (Carry, and_2_out, and_3_out, and_4_out, and_5_out, aa4_g);
endmodule

module lookahead_add32 (
  input  [31:0] A,
  input  [31:0] B,
  input  C0,
  output [31:0] result
);

  wire low_carry;

  // Probe on result
  lookahead_add16 low (.A(A[15:0]), .B(B[15:0]), .C0(C0), .Carry(low_carry), .S(result[15:0]));
  lookahead_add16 high (.A(A[31:16]), .B(B[31:16]), .C0(low_carry), .S(result[31:16]));  // open: Carry
endmodule

module ALU_plus (
  input  [1:0] op,
  input  [31:0] A,
  input  [31:0] B,
  output [31:0] result
);

  wire not_2_out;
  wire [31:0] lookahead_add32_1_result, multiplexer_1_out, not_1_out, or32_1_result;

  assign not_1_out = ~B;  // NOT_Gate not_1, 32 bits wide
  Multiplexer #(.width(32)) multiplexer_1 (.in0(not_1_out), .in1(B), .out(multiplexer_1_out), .sel(op[0]));
  not not_2 (not_2_out, op[0]);
  or32 or32_1 (.A(A), .B(B), .result(or32_1_result));
  lookahead_add32 lookahead_add32_1 (.A(A), .B(multiplexer_1_out), .C0(not_2_out), .result(lookahead_add32_1_result));
  add32 add32_1 ();  // open: A, B, C0, result
  Multiplexer #(.width(32)) multiplexer_2 (
    .in0(or32_1_result), .in1(lookahead_add32_1_result), .out(result), .sel(op[1]));
endmodule

module IFU_plus (
  input  IfBeq,
  input  Zero,
  input  Reset,
  input  Clk,
  output [31:0] Instr
);

  wire and_1_out;
  wire [31:0] alu_2_result, alu_plus_1_result, bit_extender_1_out, multiplexer_1_out, PC_q;

  Register #(.width(32)) PC (.D(alu_plus_1_result), .en(1'b1), .clk(Clk), .Q(PC_q), .clr(Reset));
  ALU_plus alu_plus_1 (.op(2'b11), .A(PC_q), .B(alu_2_result), .result(alu_plus_1_result));
  ALU alu_1 ();  // open: op, A, B, result
  ROM #(.addrWidth(5), .dataWidth(32)) rom_1 (.addr(PC_q[4:0]), .data(Instr));
  and and_1 (and_1_out, IfBeq, Zero);
  Multiplexer #(.width(32)) multiplexer_1 (
    .in0(32'h1), .in1(bit_extender_1_out), .out(multiplexer_1_out), .sel(and_1_out));
  assign bit_extender_1_out = {{16{Instr[15]}}, Instr[15:0]};  // Bit_Extender bit_extender_1
  // Probe on Instr
  ALU alu_2 (.op(2'b11), .A(multiplexer_1_out), .B({32{1'b0}}), .result(alu_2_result));

  // Notes on the sheet:
  //   contents of rom_1 (hex, n*v repeats v):
  //   341d000c 34021234 34033456 432021 643023 ac020000 ac030004 afa40004 8c050000 10450001 8fa30004
  //   8c050004 1065fffd c23023 afa6fffc 1064ffff
endmodule

module main_plus (
);

  wire button_1_out, clock_1_out, controller_1_alusrc, controller_1_extop, controller_1_luiop,
       controller_1_memtoreg, controller_1_memwrite, controller_1_npc_sel, controller_1_regdst,
       controller_1_regwrite, iszero_1_z;
  wire [1:0] controller_1_aluop;
  wire [4:0] alu_plus_1_result, ifu_offset_1_plus_1_instr_4, ifu_offset_1_plus_1_instr_5, multiplexer_1_out;
  wire [5:0] ifu_offset_1_plus_1_instr_2;
  wire [15:6] ifu_offset_1_plus_1_instr_3;
  wire [26:0] alu_plus_1_result_2;
  wire [31:0] dm_1_memout, ext_1_result, gpr_1_rddata1, gpr_1_rddata2, multiplexer_2_out, multiplexer_3_out;
  wire [31:26] ifu_offset_1_plus_1_instr;

  Clock clock_1 (.out(clock_1_out));
  Button button_1 (.out(button_1_out));
  // Probe on gpr_1_rddata1
  // Probe on multiplexer_2_out
  // Probe on {alu_plus_1_result_2, alu_plus_1_result}
  // Probe on {ifu_offset_1_plus_1_instr, ifu_offset_1_plus_1_instr_5, ifu_offset_1_plus_1_instr_4, ifu_offset_1_plus_1_instr_3, ifu_offset_1_plus_1_instr_2}
  // Probe on {ifu_offset_1_plus_1_instr, ifu_offset_1_plus_1_instr_5, ifu_offset_1_plus_1_instr_4, ifu_offset_1_plus_1_instr_3, ifu_offset_1_plus_1_instr_2}
  IFU_OFFSET_1_PLUS ifu_offset_1_plus_1 (
    .IfBeq(controller_1_npc_sel), .Zero(iszero_1_z), .Reset(button_1_out), .Clk(clock_1_out),
    .Instr({ifu_offset_1_plus_1_instr, ifu_offset_1_plus_1_instr_5, ifu_offset_1_plus_1_instr_4, ifu_offset_1_plus_1_instr_3, ifu_offset_1_plus_1_instr_2}));
  IFU ifu_1 ();  // open: IfBeq, Zero, Reset, Clk, Instr
  IFU_OFFSET_1 ifu_offset_1_1 ();  // open: IfBeq, Zero, Reset, Clk, Instr
  // Probe on ext_1_result
  Multiplexer #(.width(5)) multiplexer_1 (
    .in0(ifu_offset_1_plus_1_instr_4), .in1(ifu_offset_1_plus_1_instr_3[15:11]), .out(multiplexer_1_out),
    .sel(controller_1_regdst));
  EXT ext_1 (
    .A({ifu_offset_1_plus_1_instr_3, ifu_offset_1_plus_1_instr_2}), .Extop(controller_1_extop),
    .LuiOp(controller_1_luiop), .result(ext_1_result));
  Controller controller_1 (
    .op(ifu_offset_1_plus_1_instr), .func(ifu_offset_1_plus_1_instr_2), .RegDst(controller_1_regdst),
    .ALUSrc(controller_1_alusrc), .MemtoReg(controller_1_memtoreg), .RegWrite(controller_1_regwrite),
    .MemWrite(controller_1_memwrite), .nPC_sel(controller_1_npc_sel), .ExtOp(controller_1_extop),
    .LuiOp(controller_1_luiop), .ALUop(controller_1_aluop));
  // Probe on gpr_1_rddata2
  GPR gpr_1 (
    .Regrd1(ifu_offset_1_plus_1_instr_5), .Regrd2(ifu_offset_1_plus_1_instr_4), .A3(multiplexer_1_out),
    .clk(clock_1_out), .Reset(button_1_out), .Regwrite(controller_1_regwrite), .Wd(multiplexer_3_out),
    .Rddata1(gpr_1_rddata1), .Rddata2(gpr_1_rddata2));
  Multiplexer #(.width(32)) multiplexer_2 (
    .in0(gpr_1_rddata2), .in1(ext_1_result), .out(multiplexer_2_out), .sel(controller_1_alusrc));
  // Probe on ext_1_result
  // Probe on gpr_1_rddata1
  // Probe on multiplexer_2_out
  // Probe on multiplexer_2_out
  IsZero iszero_1 (.A({alu_plus_1_result_2, alu_plus_1_result}), .Z(iszero_1_z));
  ALU_plus alu_plus_1 (
    .op(controller_1_aluop), .A(gpr_1_rddata1), .B(multiplexer_2_out),
    .result({alu_plus_1_result_2, alu_plus_1_result}));
  ALU alu_1 ();  // open: op, A, B, result
  // Probe on {alu_plus_1_result_2, alu_plus_1_result}
  DM dm_1 (
    .address(alu_plus_1_result), .Data(gpr_1_rddata2), .Memtoreg(controller_1_memtoreg),
    .Memwrite(controller_1_memwrite), .Clk(clock_1_out), .Reset(button_1_out), .MEMout(dm_1_memout));
  Multiplexer #(.width(32)) multiplexer_3 (
    .in0({alu_plus_1_result_2, alu_plus_1_result}), .in1(dm_1_memout), .out(multiplexer_3_out),
    .sel(controller_1_memtoreg));
endmodule

module IFU_OFFSET_1_PLUS (
  input  IfBeq,
  input  Zero,
  input  Reset,
  input  Clk,
  output [31:0] Instr
);

  wire and_1_out;
  wire [31:0] alu_2_result, alu_plus_1_result, bit_extender_1_out, multiplexer_1_out, PC_q;

  Register #(.width(32)) PC (.D(multiplexer_1_out), .en(1'b1), .clk(Clk), .Q(PC_q), .clr(Reset));
  ALU_plus alu_plus_1 (.op(2'b11), .A(PC_q), .B(32'h1), .result(alu_plus_1_result));
  ALU alu_1 ();  // open: op, A, B, result
  ROM #(.addrWidth(5), .dataWidth(32)) rom_1 (.addr(PC_q[4:0]), .data(Instr));
  and and_1 (and_1_out, IfBeq, Zero);
  Multiplexer #(.width(32)) multiplexer_1 (
    .in0(alu_plus_1_result), .in1(alu_2_result), .out(multiplexer_1_out), .sel(and_1_out));
  assign bit_extender_1_out = {{16{Instr[15]}}, Instr[15:0]};  // Bit_Extender bit_extender_1
  // Probe on Instr
  ALU alu_2 (.op(2'b11), .A(alu_plus_1_result), .B(bit_extender_1_out), .result(alu_2_result));

  // Notes on the sheet:
  //   contents of rom_1 (hex, n*v repeats v):
  //   341d000c 34021234 34033456 432021 643023 ac020000 ac030004 afa40004 8c050000 10450001 8fa30004
  //   8c050004 1065fffd c23023 afa6fffc 1064ffff
endmodule
